// Digital circuit 数字钟.dig as structural Verilog
module \数字钟  (
  input  clk,
  input  \_12_24小时制 ,
  input  Set,
  input  \闹钟 ,
  input  \秒表 
);

  wire _3, _4, _5, _8, not_1_out, not_3_out, register_1_q, register_2_q, register_3_q, register_4_q,
       register_5_q, register_6_q, \合并_1_p13 , \秒表_1_p1 , \闹钟_1_p9 ;
  wire [3:0] multiplexer_1_out, multiplexer_2_out, multiplexer_3_out, multiplexer_4_out, multiplexer_5_out,
       multiplexer_6_out, multiplexer_7_out, multiplexer_8_out, multiplexer_9_out, multiplexer_10_out,
       multiplexer_11_out, multiplexer_12_out, \合并_1_p7 , \合并_1_p8 , \合并_1_p9 , \合并_1_p10 , \合并_1_p11 ,
       \合并_1_p12 , \秒表_1_p4 , \秒表_1_p5 , \秒表_1_p6 , \秒表_1_p7 , \秒表_1_p8 , \秒表_1_p9 , \闹钟_1_p10 , \闹钟_1_p11 ,
       \闹钟_1_p12 , \闹钟_1_p13 , \闹钟_1_p14 , \闹钟_1_p15 ;
  wire [15:0] multiplexer_13_out, multiplexer_14_out, multiplexer_15_out;

  Button \u_时  (.out(_5));
  Button \u_分  (.out(_4));
  Button \u_秒  (.out(_3));
  Button Reset (.out(_8));
  Register register_1 (.D(_3), .C(clk), .en(Set), .Q(register_1_q));
  Register register_2 (.D(_4), .C(clk), .en(Set), .Q(register_2_q));
  Register register_3 (.D(_5), .C(clk), .en(Set), .Q(register_3_q));
  not not_1 (not_1_out, Set);
  // 合并 合并_1: pin names not known; wires that end beside it: clk, register_1_q, register_2_q, register_3_q, \_12_24小时制 , not_1_out, \合并_1_p7 , \合并_1_p8 , \合并_1_p9 , \合并_1_p10 , \合并_1_p11 , \合并_1_p12 , \合并_1_p13 
  Register register_4 (.D(_3), .C(clk), .en(\闹钟 ), .Q(register_4_q));
  Register register_5 (.D(_4), .C(clk), .en(\闹钟 ), .Q(register_5_q));
  Register register_6 (.D(_5), .C(clk), .en(\闹钟 ), .Q(register_6_q));
  // 秒表 秒表_1: pin names not known; wires that end beside it: \秒表_1_p1 , _8, clk, \秒表_1_p4 , \秒表_1_p5 , \秒表_1_p6 , \秒表_1_p7 , \秒表_1_p8 , \秒表_1_p9 
  not not_2 (\秒表_1_p1 , not_3_out);
  Multiplexer #(.Bits(4)) multiplexer_1 (.sel(\闹钟 ), .in_0(\合并_1_p12 ), .in_1(\闹钟_1_p15 ), .out(multiplexer_1_out));
  // 闹钟 闹钟_1: pin names not known; wires that end beside it: \合并_1_p9 , \合并_1_p10 , \合并_1_p11 , \合并_1_p12 , clk, register_4_q, register_5_q, register_6_q, \闹钟_1_p9 , \闹钟_1_p10 , \闹钟_1_p11 , \闹钟_1_p12 , \闹钟_1_p13 , \闹钟_1_p14 , \闹钟_1_p15 
  Seven_Seg_Hex seven_seg_hex_1 (.d(multiplexer_2_out), .dp(1'b0));
  Multiplexer #(.Bits(4)) multiplexer_2 (
    .sel(not_3_out), .in_0(\秒表_1_p9 ), .in_1(multiplexer_1_out), .out(multiplexer_2_out));
  Multiplexer #(.Bits(4)) multiplexer_3 (.sel(\闹钟 ), .in_0(\合并_1_p11 ), .in_1(\闹钟_1_p14 ), .out(multiplexer_3_out));
  Multiplexer #(.Bits(4)) multiplexer_4 (
    .sel(not_3_out), .in_0(\秒表_1_p8 ), .in_1(multiplexer_3_out), .out(multiplexer_4_out));
  Seven_Seg_Hex seven_seg_hex_2 (.d(multiplexer_4_out), .dp(1'b0));
  Multiplexer #(.Bits(4)) multiplexer_5 (.sel(\闹钟 ), .in_0(\合并_1_p10 ), .in_1(\闹钟_1_p13 ), .out(multiplexer_5_out));
  Seven_Seg_Hex seven_seg_hex_3 (.d(multiplexer_6_out), .dp(1'b0));
  Multiplexer #(.Bits(4)) multiplexer_6 (
    .sel(not_3_out), .in_0(\秒表_1_p7 ), .in_1(multiplexer_5_out), .out(multiplexer_6_out));
  Multiplexer #(.Bits(4)) multiplexer_7 (.sel(\闹钟 ), .in_0(\合并_1_p9 ), .in_1(\闹钟_1_p12 ), .out(multiplexer_7_out));
  Seven_Seg_Hex seven_seg_hex_4 (.d(multiplexer_8_out), .dp(1'b0));
  Multiplexer #(.Bits(4)) multiplexer_8 (
    .sel(not_3_out), .in_0(\秒表_1_p6 ), .in_1(multiplexer_7_out), .out(multiplexer_8_out));
  Multiplexer #(.Bits(4)) multiplexer_9 (.sel(\闹钟 ), .in_0(\合并_1_p8 ), .in_1(\闹钟_1_p11 ), .out(multiplexer_9_out));
  Multiplexer #(.Bits(4)) multiplexer_10 (
    .sel(not_3_out), .in_0(\秒表_1_p5 ), .in_1(multiplexer_9_out), .out(multiplexer_10_out));
  Multiplexer #(.Bits(4)) multiplexer_11 (.sel(\闹钟 ), .in_0(\合并_1_p7 ), .in_1(\闹钟_1_p10 ), .out(multiplexer_11_out));
  Seven_Seg_Hex seven_seg_hex_5 (.d(multiplexer_10_out), .dp(1'b0));
  Seven_Seg_Hex seven_seg_hex_6 (.d(multiplexer_12_out), .dp(1'b0));
  Multiplexer #(.Bits(4)) multiplexer_12 (
    .sel(not_3_out), .in_0(\秒表_1_p4 ), .in_1(multiplexer_11_out), .out(multiplexer_12_out));
  not not_3 (not_3_out, \秒表 );
  Multiplexer #(.Bits(16)) multiplexer_13 (.sel(\合并_1_p13 ), .in_0(16'h3c7), .in_1(16'h3cf), .out(multiplexer_13_out));
  SixteenSeg sixteenseg_1 (.led(multiplexer_14_out), .dp(1'b0));
  Multiplexer #(.Bits(16)) multiplexer_14 (
    .sel(\_12_24小时制 ), .in_0({16{1'b0}}), .in_1(multiplexer_13_out), .out(multiplexer_14_out));
  SixteenSeg sixteenseg_2 (.led(multiplexer_15_out), .dp(1'b0));
  Multiplexer #(.Bits(16)) multiplexer_15 (
    .sel(\_12_24小时制 ), .in_0({16{1'b0}}), .in_1(16'h14cc), .out(multiplexer_15_out));
  LED led_1 (.in(\闹钟_1_p9 ));

  // Other names for the same wires on the sheet: _1 = \_12_24小时制 ; _2 = Set; _6 = \闹钟 ; _7 = \秒表 

  // Notes on the sheet:
  //   clk: Hz: 5000
endmodule
