// Digital circuit 自动售货机.dig as structural Verilog
module \自动售货机  (
  input  T2,
  input  T1,
  input  T0,
  input  CLK,
  input  EN,
  output L2,
  output L1,
  output L3,
  output L0,
  output \是否出饮料 
);

  wire A0_q, A1_q, A2_q, A3_q, A4_q, and_1_out, and_2_out, and_3_out, and_4_out, and_5_out, and_6_out,
       and_7_out, and_8_out, and_9_out, and_10_out, and_11_out, and_12_out, and_13_out, and_14_out,
       and_15_out, and_16_out, or_1_out, or_2_out, or_3_out, or_4_out, or_5_out, or_6_out;

  and and_1 (and_1_out, ~L3, ~L2, ~L1, ~L0, ~A4_q, ~A3_q, ~A2_q, ~A1_q, ~A0_q);  // And
  and and_2 (and_2_out, T0, A0_q);
  and and_3 (and_3_out, T0, A1_q);
  and and_4 (and_4_out, T1, A0_q);
  and and_5 (and_5_out, T0, A2_q);
  and and_6 (and_6_out, T1, A1_q);
  and and_7 (and_7_out, T0, A3_q);
  and and_8 (and_8_out, T1, A2_q);
  and and_9 (and_9_out, T2, A0_q);
  and and_10 (and_10_out, T0, A4_q);
  and and_11 (and_11_out, T1, A3_q);
  and and_12 (and_12_out, T2, A1_q);
  and and_13 (and_13_out, T1, A4_q);
  and and_14 (and_14_out, T2, A2_q);
  or or_1 (or_1_out, L3, L2, L1, L0, and_1_out);
  or or_2 (or_2_out, and_3_out, and_4_out);
  or or_3 (or_3_out, and_5_out, and_6_out);
  or or_4 (or_4_out, and_7_out, and_8_out, and_9_out);
  and and_15 (and_15_out, T2, A3_q);
  and and_16 (and_16_out, T2, A4_q);
  or or_5 (or_5_out, and_10_out, and_11_out, and_12_out);
  or or_6 (or_6_out, and_13_out, and_14_out);
  Register A0 (.D(or_1_out), .C(CLK), .en(EN), .Q(A0_q));
  Register A1 (.D(and_2_out), .C(CLK), .en(EN), .Q(A1_q));
  Register A2 (.D(or_2_out), .C(CLK), .en(EN), .Q(A2_q));
  Register A3 (.D(or_3_out), .C(CLK), .en(EN), .Q(A3_q));
  Register A4 (.D(or_4_out), .C(CLK), .en(EN), .Q(A4_q));
  Register A5 (.D(or_5_out), .C(CLK), .en(EN), .Q(L0));
  Register A6 (.D(or_6_out), .C(CLK), .en(EN), .Q(L1));
  Register A7 (.D(and_15_out), .C(CLK), .en(EN), .Q(L2));
  Register A8 (.D(and_16_out), .C(CLK), .en(EN), .Q(L3));
  or or_7 (\是否出饮料 , L3, L2, L1, L0);
endmodule
